// Logisim project x69_lamda_b01.circ as structural Verilog
module main (
);

  wire aludecoder_1_flagen, aludecoder_1_ien, and_1_out, and_2_out, and_3_out, and_4_out, bitfinder_1_found,
       buffer_1_out, buffer_2_out, buffer_3_out, buffer_4_out, buffer_5_out, buffer_6_out, buffer_7_out,
       button_1_out, button_2_out, button_3_out, clock_1_out, decoder_1_out0, decoder_1_out1, decoder_1_out2,
       decoder_1_out3, decoder_2_out0, decoder_2_out1, decoder_2_out2, memio_1_done, memio_1_mclk,
       memio_1_men, memio_1_mr, memio_1_mw, memio_2_mclk, memio_3_done, memio_3_mclk, memio_3_mr, memio_3_mw,
       not_1_out, not_2_out, not_3_out, not_4_out, not_5_out, not_6_out, not_7_out, or_2_out, POR, por_1_out,
       s_r_ff_1_q, switch_1_p2, t_ff_1_q, t_ff_1_qn, t_ff_2_q, t_ff_2_qn;
  wire [0:0] register_4_q;
  wire [1:0] bitfinder_1_index, counter_1_q;
  wire [3:0] aludecoder_1_rb, aludecoder_1_rd, pull_resistor_1_node, pull_resistor_2_node,
       pull_resistor_3_node, pull_resistor_4_node, pull_resistor_5_node;
  wire [4:0] aludecoder_1_op, register_4_q_2;
  wire [5:0] alu_1_flg;
  wire [15:0] alu_1_q, aludecoder_1_im, counter_2_q, memio_1_maddr, memio_1_mdin, memio_2_maddr,
       memio_3_dout, memio_3_maddr, memio_3_mdin, multiplexer_1_out, pull_resistor_6_node,
       pull_resistor_8_node, ram_1_dout, reg16_1_ro0, reg16_1_ro1, reg16_1_ro2, reg16_1_ro3, register_1_q,
       register_2_q, register_3_q, rom_1_data;

  Button button_1 (.out(button_1_out));
  Clock clock_1 (.out(clock_1_out));
  POR #(.PorHighDuration(1)) por_1 (.out(por_1_out));
  T_Flip_Flop t_ff_1 (.clk(button_1_out), .T(1'b1), .Q(t_ff_1_q), .Qn(t_ff_1_qn), .reset(por_1_out));  // open: preset
  S_R_Flip_Flop s_r_ff_1 (
    .S(t_ff_1_q), .clk(clock_1_out), .R(t_ff_1_qn), .Q(s_r_ff_1_q), .reset(por_1_out));  // open: Qn, preset
  not not_1 (not_1_out, s_r_ff_1_q);
  not not_2 (not_2_out, not_1_out);
  BitFinder #(.width(4)) bitfinder_1 (.in(register_1_q[3:0]), .index(bitfinder_1_index), .found(bitfinder_1_found));
  and and_1 (and_1_out, clock_1_out, s_r_ff_1_q);
  and and_2 (and_2_out, not_2_out, not_1_out);
  Decoder #(.select(2)) decoder_1 (
    .out0(decoder_1_out0), .out1(decoder_1_out1), .out2(decoder_1_out2), .out3(decoder_1_out3),
    .sel(bitfinder_1_index), .en(bitfinder_1_found));
  or or_1 (POR, and_2_out, por_1_out);
  // Probe on pull_resistor_1_node
  // Probe on pull_resistor_2_node
  // Probe on pull_resistor_3_node
  Button button_2 (.out(button_2_out));
  Pull_Resistor pull_resistor_1 (.node(pull_resistor_1_node));
  Pull_Resistor pull_resistor_2 (.node(pull_resistor_2_node));
  Button button_3 (.out(button_3_out));
  Decoder #(.select(2)) decoder_2 (
    .out0(decoder_2_out0), .out1(decoder_2_out1), .out2(decoder_2_out2), .sel(counter_1_q), .en(button_2_out));  // open: out3
  Counter #(.max('h3), .trigger("falling"), .width(2)) counter_1 (
    .Q(counter_1_q), .clk(button_2_out));  // open: load, D, count, carry, up, clr
  Pull_Resistor pull_resistor_3 (.node(pull_resistor_3_node));
  Pull_Resistor pull_resistor_4 (.node(pull_resistor_4_node));
  Pull_Resistor pull_resistor_5 (.node(pull_resistor_5_node));
  Reg16 reg16_1 (
    .Ro2(reg16_1_ro2), .Ro0(reg16_1_ro0), .Ro1(reg16_1_ro1), .Ro3(reg16_1_ro3), .DIn(pull_resistor_8_node),
    .W(and_4_out), .En(t_ff_2_qn), .Wsel(pull_resistor_3_node), .Rst(POR), .Rs0(pull_resistor_1_node),
    .Rs1(pull_resistor_2_node), .Rs2(pull_resistor_4_node), .Rs3(pull_resistor_5_node));
  Reg16 reg16_2 (
    .Ro2(reg16_1_ro2), .Ro0(reg16_1_ro0), .Ro1(reg16_1_ro1), .Ro3(reg16_1_ro3), .DIn(pull_resistor_8_node),
    .W(and_4_out), .En(t_ff_2_q), .Wsel(pull_resistor_3_node), .Rst(POR), .Rs0(pull_resistor_1_node),
    .Rs1(pull_resistor_2_node), .Rs2(pull_resistor_4_node), .Rs3(pull_resistor_5_node));
  T_Flip_Flop t_ff_2 (.clk(button_3_out), .T(1'b1), .Q(t_ff_2_q), .Qn(t_ff_2_qn), .reset(POR));  // open: preset
  or or_2 (or_2_out, decoder_2_out1, decoder_2_out0);
  Transistor #(.gate("br"), .\type ("n"), .width(4)) transistor_1 (
    .in(aludecoder_1_rd), .out(pull_resistor_3_node), .gate(decoder_1_out0));
  Counter #(.max('hffff), .trigger("falling"), .width(16)) counter_2 (
    .D({16{1'b0}}), .count(1'b1), .Q(counter_2_q), .up(1'b1), .clk(or_2_out), .clr(POR));  // open: load, carry
  not not_3 (not_3_out, decoder_2_out2);
  Transistor #(.gate("br"), .\type ("n"), .width(4)) transistor_2 (
    .in(aludecoder_1_rb), .out(pull_resistor_2_node), .gate(aludecoder_1_ien));
  Pull_Resistor #(.pull(1)) pull_resistor_6 (.node(pull_resistor_6_node));
  Transistor #(.\type ("n"), .width(16)) transistor_3 (.in(counter_2_q), .out(pull_resistor_6_node), .gate(not_3_out));
  ALUDecoder aludecoder_1 (
    .FlagEn(aludecoder_1_flagen), .Op(aludecoder_1_op), .rA(pull_resistor_1_node), .rB(aludecoder_1_rb),
    .IEn(aludecoder_1_ien), .rD(aludecoder_1_rd), .Im(aludecoder_1_im), .Ins({register_2_q, register_1_q}));
  // Probe on reg16_1_ro0
  // Probe on reg16_1_ro1
  // Probe on reg16_1_ro2
  // Probe on reg16_1_ro3
  // Probe on pull_resistor_6_node
  Multiplexer #(.enable("false"), .width(16)) multiplexer_1 (
    .in0(reg16_1_ro1), .in1(aludecoder_1_im), .out(multiplexer_1_out), .sel(aludecoder_1_ien));
  Register #(.trigger("falling"), .width(16)) register_1 (
    .D(pull_resistor_8_node), .en(1'b1), .Q(register_1_q), .clk(decoder_2_out0), .clr(POR));
  Register #(.trigger("falling"), .width(16)) register_2 (
    .D(pull_resistor_8_node), .en(1'b1), .Q(register_2_q), .clk(decoder_2_out1), .clr(POR));
  // Probe on alu_1_q
  // Probe on aludecoder_1_op
  Pull_Resistor pull_resistor_7 (.node({register_2_q, register_1_q}));
  ALU alu_1 (
    .Q(alu_1_q), .Flg(alu_1_flg), .Cin(register_4_q[0]), .En(1'b1), .A(reg16_1_ro0), .B(multiplexer_1_out),
    .Op(aludecoder_1_op));
  and and_3 (and_3_out, decoder_2_out2, decoder_1_out0);
  not not_4 (not_4_out, aludecoder_1_flagen);
  // Probe on {register_2_q, register_1_q}
  // Probe on pull_resistor_8_node
  Register #(.width(16)) register_3 (.D(alu_1_q), .en(decoder_1_out0), .Q(register_3_q), .clk(and_3_out), .clr(POR));
  Register #(.width(6)) register_4 (
    .D(alu_1_flg), .en(not_4_out), .Q({register_4_q_2, register_4_q[0]}), .clk(and_3_out), .clr(POR));
  not not_5 (not_5_out, and_3_out);
  not not_6 (not_6_out, not_5_out);
  Pull_Resistor #(.pull(1)) pull_resistor_8 (.node(pull_resistor_8_node));
  Transistor #(.\type ("n"), .width(16)) transistor_4 (
    .in(register_3_q), .out(pull_resistor_8_node), .gate(decoder_1_out0));
  // Probe on pull_resistor_8_node
  and and_4 (and_4_out, not_6_out, not_5_out);
  // Switch switch_1: pin names not known; wires that end beside it: 1'b1, switch_1_p2
  Pull_Resistor pull_resistor_9 (.node(switch_1_p2));
  not not_7 (not_7_out, switch_1_p2);
  MemIO memio_1 (
    .Done(memio_1_done), .DOut(pull_resistor_8_node), .MClk(memio_1_mclk), .MAddr(memio_1_maddr),
    .MDin(memio_1_mdin), .MR(memio_1_mr), .MW(memio_1_mw), .MEn(memio_1_men), .En(switch_1_p2),
    .Clk(or_2_out), .Addr(pull_resistor_6_node), .DIn(pull_resistor_8_node), .Read(or_2_out), .Write(1'b0),
    .MDn(memio_3_done), .MDout(memio_3_dout));
  MemIO memio_2 (
    .Done(memio_1_done), .DOut(pull_resistor_8_node), .MClk(memio_2_mclk), .MAddr(memio_2_maddr),
    .En(not_7_out), .Clk(or_2_out), .Addr(pull_resistor_6_node), .DIn(pull_resistor_8_node), .Read(or_2_out),
    .Write(1'b0), .MDn(buffer_3_out), .MDout(rom_1_data));  // open: MDin, MR, MW, MEn
  buf buffer_1 (buffer_1_out, memio_2_mclk);
  buf buffer_2 (buffer_2_out, buffer_1_out);
  ROM #(.dataWidth(16)) rom_1 (.addr(memio_2_maddr[7:0]), .data(rom_1_data));
  buf buffer_3 (buffer_3_out, buffer_2_out);
  MemIO memio_3 (
    .Done(memio_3_done), .DOut(memio_3_dout), .MClk(memio_3_mclk), .MAddr(memio_3_maddr),
    .MDin(memio_3_mdin), .MR(memio_3_mr), .MW(memio_3_mw), .En(memio_1_men), .Clk(memio_1_mclk),
    .Addr(memio_1_maddr), .DIn(memio_1_mdin), .Read(memio_1_mr), .Write(memio_1_mw), .MDn(buffer_7_out),
    .MDout(ram_1_dout));  // open: MEn
  buf buffer_4 (buffer_4_out, memio_3_mclk);
  buf buffer_5 (buffer_5_out, buffer_4_out);
  buf buffer_6 (buffer_6_out, buffer_5_out);
  buf buffer_7 (buffer_7_out, buffer_6_out);
  RAM #(.addrWidth(16), .dataWidth(16)) ram_1 (
    .addr(memio_3_maddr), .we(memio_3_mw), .oe(memio_3_mr), .clk(memio_3_mclk), .din(memio_3_mdin),
    .dout(ram_1_dout));

  // Notes on the sheet:
  //   Addr
  //   Data
  //   Ins
  //   Clk
  //   Clk
  //   Ra
  //   Rb
  //   Registers -> Address Bus
  //   Registers -> Data Bus
  //   Rd
  //   Write Result
  //   Interrupt
  //   Standard
  //   PC
  //   Instruction
  //   ALU Enable
  //   Clk
  //   rD
  //   No Flags
  //   Op Code
  //   rB
  //   Immediate
  //   rA
  //   Use Immediate
  //   Use Immediate
  //   Clk
  //   Op Code
  //   Clk
  //   ALU En
  //   Write Result
  //   ALU Result
  //   ALU Flags
  //   Addr
  //   Ins
  //   Data
  //   Boot Loader
  //   IO "Delay"
  //   contents of rom_1 (hex, n*v repeats v):
  //   0 71 0 71 0 71 0 71 0 71 0 71 0 71 0 71 0 71 0 71 1f0f f064 8831 6a3e 3b18 b817 e8ce 9020 1d30 6da9
  //   4568 a440 e82a 113d 9444 4365 a526 f037 b6b5 f795 be77 c22a a76c 535c 9ac4 4a2 f941 4336 472f 5793
  //   9dc5 529b 5bc6 6571 3afb 5272 56a2 bf50 f9b6 d006 d3e1 9657 28b1 5fc2 938c a36b 75a5 fae3 b683 1369
  //   dbaf bc2b 1146 5d10 e7a7 a316 bab8 5cf1 258e bfca ee72 868c a096 29d0 11ee efa0 6f4b 6161 c9ea 2ed0
  //   89d5 8426 f67b a821 3edc f40b 8811 d416 c6f7 6649 1b24 2868 dcc3 9356 52c8 968f 2b13 b60 f911 943b
  //   8170 b782 f6ad 875a 6389 d32b 75df 61bd e85d 4499 c062 9310 5473 1c09 1fc7 a10 253a 289c c4fd 4aa5
  //   c509 54f7 4a0a 1d52 1da6 4603 10e8 b881 24b4 409e a80b 9c76 182a f940 90cc 82f9 e3a3 c79a a1dd 82d7
  //   6791 10d a854 d893 9409 857e 8121 187e 57c1 f2ae 52db 5c3 cb5c 7146 c178 fd6c 27b4 ac74 5a56 1f03
  //   854f 9f36 43ea dd6e a40 6a2a a90d dd7c 9c4b 1f61 e108 634d ddb1 3834 fafa a79a c5a1 6951 d9a3 515c
  //   8883 8389 3bd1 c246 61c7 9a85 f268 9caf afb6 6dd9 af19 d2a1 5b4f aca 9aae 78c c977 5e82 97d2 2b76
  //   416e 5e98 5b4f fed4 6532 21f 758b dcc7 c53d 4d06 ee5e 6d7c e03a 8bdf 14ef 1f1a c315 c3f3 ccfc d051
  //   a49e 94ea a21f 7f7e ba3 f270 b4c3 13a1 7dda 677e a370 2467 329d 6a2 a265 ab85 8575 dc92 4353 9ec9
  //   c334 1995 385 e6df a7c2 3424
  //   Outside World Memory Interface
  //   Memory IO "Delay"
  //   RAM
endmodule

module Reg16 (
  input  [15:0] DIn,
  input  W,
  input  En,
  input  [3:0] Wsel,
  input  Rst,
  input  [3:0] Rs0,
  input  [3:0] Rs1,
  input  [3:0] Rs2,
  input  [3:0] Rs3,
  output [15:0] Ro0,
  output [15:0] Ro1,
  output [15:0] Ro2,
  output [15:0] Ro3
);

  wire decoder_1_out0, decoder_1_out1, decoder_1_out2, decoder_1_out3, decoder_1_out4, decoder_1_out5,
       decoder_1_out6, decoder_1_out7, decoder_1_out8, decoder_1_out9, decoder_1_out10, decoder_1_out11,
       decoder_1_out12, decoder_1_out13, decoder_1_out14, decoder_1_out15;
  wire [15:0] multiplexer_1_out, multiplexer_2_out, multiplexer_3_out, multiplexer_4_out, register_1_q,
       register_2_q, register_3_q, register_4_q, register_5_q, register_6_q, register_7_q, register_8_q,
       register_9_q, register_10_q, register_11_q, register_12_q, register_13_q, register_14_q,
       register_15_q, register_16_q;

  Decoder #(.select(4)) decoder_1 (
    .out0(decoder_1_out0), .out1(decoder_1_out1), .out2(decoder_1_out2), .out3(decoder_1_out3),
    .out4(decoder_1_out4), .out5(decoder_1_out5), .out6(decoder_1_out6), .out7(decoder_1_out7),
    .out8(decoder_1_out8), .out9(decoder_1_out9), .out10(decoder_1_out10), .out11(decoder_1_out11),
    .out12(decoder_1_out12), .out13(decoder_1_out13), .out14(decoder_1_out14), .out15(decoder_1_out15),
    .sel(Wsel), .en(En));
  Register #(.width(16)) register_1 (.D(DIn), .en(decoder_1_out0), .Q(register_1_q), .clk(W), .clr(Rst));
  Register #(.width(16)) register_2 (.D(DIn), .en(decoder_1_out1), .Q(register_2_q), .clk(W), .clr(Rst));
  Register #(.width(16)) register_3 (.D(DIn), .en(decoder_1_out2), .Q(register_3_q), .clk(W), .clr(Rst));
  Register #(.width(16)) register_4 (.D(DIn), .en(decoder_1_out3), .Q(register_4_q), .clk(W), .clr(Rst));
  Register #(.width(16)) register_5 (.D(DIn), .en(decoder_1_out4), .Q(register_5_q), .clk(W), .clr(Rst));
  Register #(.width(16)) register_6 (.D(DIn), .en(decoder_1_out5), .Q(register_6_q), .clk(W), .clr(Rst));
  Register #(.width(16)) register_7 (.D(DIn), .en(decoder_1_out6), .Q(register_7_q), .clk(W), .clr(Rst));
  Register #(.width(16)) register_8 (.D(DIn), .en(decoder_1_out7), .Q(register_8_q), .clk(W), .clr(Rst));
  Register #(.width(16)) register_9 (.D(DIn), .en(decoder_1_out8), .Q(register_9_q), .clk(W), .clr(Rst));
  Register #(.width(16)) register_10 (.D(DIn), .en(decoder_1_out9), .Q(register_10_q), .clk(W), .clr(Rst));
  Register #(.width(16)) register_11 (.D(DIn), .en(decoder_1_out10), .Q(register_11_q), .clk(W), .clr(Rst));
  Register #(.width(16)) register_12 (.D(DIn), .en(decoder_1_out11), .Q(register_12_q), .clk(W), .clr(Rst));
  Register #(.width(16)) register_13 (.D(DIn), .en(decoder_1_out12), .Q(register_13_q), .clk(W), .clr(Rst));
  Register #(.width(16)) register_14 (.D(DIn), .en(decoder_1_out13), .Q(register_14_q), .clk(W), .clr(Rst));
  Register #(.width(16)) register_15 (.D(DIn), .en(decoder_1_out14), .Q(register_15_q), .clk(W), .clr(Rst));
  Register #(.width(16)) register_16 (.D(DIn), .en(decoder_1_out15), .Q(register_16_q), .clk(W), .clr(Rst));
  Multiplexer #(.enable("false"), .select(4), .width(16)) multiplexer_1 (
    .in0(register_1_q), .in1(register_2_q), .in2(register_3_q), .in3(register_4_q), .in4(register_5_q),
    .in5(register_6_q), .in6(register_7_q), .in7(register_8_q), .in8(register_9_q), .in9(register_10_q),
    .in10(register_11_q), .in11(register_12_q), .in12(register_13_q), .in13(register_14_q),
    .in14(register_15_q), .in15(register_16_q), .out(multiplexer_1_out), .sel(Rs0));
  Multiplexer #(.enable("false"), .select(4), .width(16)) multiplexer_2 (
    .in0(register_1_q), .in1(register_2_q), .in2(register_3_q), .in3(register_4_q), .in4(register_5_q),
    .in5(register_6_q), .in6(register_7_q), .in7(register_8_q), .in8(register_9_q), .in9(register_10_q),
    .in10(register_11_q), .in11(register_12_q), .in12(register_13_q), .in13(register_14_q),
    .in14(register_15_q), .in15(register_16_q), .out(multiplexer_2_out), .sel(Rs1));
  Multiplexer #(.enable("false"), .select(4), .width(16)) multiplexer_3 (
    .in0(register_1_q), .in1(register_2_q), .in2(register_3_q), .in3(register_4_q), .in4(register_5_q),
    .in5(register_6_q), .in6(register_7_q), .in7(register_8_q), .in8(register_9_q), .in9(register_10_q),
    .in10(register_11_q), .in11(register_12_q), .in12(register_13_q), .in13(register_14_q),
    .in14(register_15_q), .in15(register_16_q), .out(multiplexer_3_out), .sel(Rs2));
  Multiplexer #(.enable("false"), .select(4), .width(16)) multiplexer_4 (
    .in0(register_1_q), .in1(register_2_q), .in2(register_3_q), .in3(register_4_q), .in4(register_5_q),
    .in5(register_6_q), .in6(register_7_q), .in7(register_8_q), .in8(register_9_q), .in9(register_10_q),
    .in10(register_11_q), .in11(register_12_q), .in12(register_13_q), .in13(register_14_q),
    .in14(register_15_q), .in15(register_16_q), .out(multiplexer_4_out), .sel(Rs3));
  assign Ro0 = En ? multiplexer_1_out : 16'bz;  // Controlled_Buffer controlled_buffer_1
  assign Ro1 = En ? multiplexer_2_out : 16'bz;  // Controlled_Buffer controlled_buffer_2
  assign Ro2 = En ? multiplexer_3_out : 16'bz;  // Controlled_Buffer controlled_buffer_3
  assign Ro3 = En ? multiplexer_4_out : 16'bz;  // Controlled_Buffer controlled_buffer_4
endmodule

module ALU (
  input  En,
  input  [15:0] A,
  input  [15:0] B,
  input  [4:0] Op,
  input  Cin,
  output [5:0] Flg,
  output [15:0] Q
);

  wire adder_2_cout, adder_3_cout, adder_4_cout, adder_5_cout, adder_6_cout, adder_7_cout, adder_8_cout,
       adder_9_cout, adder_10_cout, bitfinder_1_found, multiplexer_2_out, multiplexer_3_out, nor_2_out,
       nor_3_out, nor_4_out, not_5_out;
  wire [2:0] and_2_out;
  wire [3:0] pla_2_out, pla_3_out;
  wire [5:0] pla_1_out;
  wire [15:0] adder_1_out, adder_2_out, adder_3_out, adder_4_out, adder_5_out, adder_6_out, adder_7_out,
       adder_8_out, adder_9_out, adder_10_out, and_1_out, multiplexer_1_out, nand_1_out, nor_1_out,
       not_1_out, not_2_out, not_3_out, not_4_out, or_1_out, xnor_1_out, xor_1_out;

  assign not_1_out = ~A;  // NOT_Gate not_1, 16 bits wide
  assign not_2_out = ~A;  // NOT_Gate not_2, 16 bits wide
  assign not_3_out = ~B;  // NOT_Gate not_3, 16 bits wide
  Adder #(.width(16)) adder_1 (.a(not_2_out), .b(16'h1), .out(adder_1_out), .cin(1'b0));  // open: cout
  assign and_1_out = A & B;  // AND_Gate and_1, 16 bits wide
  assign nand_1_out = ~(A & B);  // NAND_Gate nand_1, 16 bits wide
  assign or_1_out = A | B;  // OR_Gate or_1, 16 bits wide
  assign nor_1_out = ~(A | B);  // NOR_Gate nor_1, 16 bits wide
  assign xor_1_out = A ^ B;  // XOR_Gate xor_1, 16 bits wide
  assign xnor_1_out = ~(A ^ B);  // XNOR_Gate xnor_1, 16 bits wide
  Adder #(.width(16)) adder_2 (.a(A), .b(B), .out(adder_2_out), .cin(1'b0), .cout(adder_2_cout));
  Adder #(.width(16)) adder_3 (.a(A), .b(B), .out(adder_3_out), .cin(Cin), .cout(adder_3_cout));
  Adder #(.width(16)) adder_4 (.a(not_3_out), .b(16'h1), .out(adder_4_out), .cout(adder_4_cout));  // open: cin
  Adder #(.width(16)) adder_5 (.a(not_3_out), .b(16'h1), .out(adder_5_out), .cin(Cin), .cout(adder_5_cout));
  assign not_4_out = ~16'h1;  // NOT_Gate not_4, 16 bits wide
  Adder #(.width(16)) adder_6 (.a(not_4_out), .b(16'h1), .out(adder_6_out), .cout(adder_6_cout));  // open: cin
  Adder #(.width(16)) adder_7 (.a(A), .b(adder_4_out), .out(adder_7_out), .cout(adder_7_cout));  // open: cin
  Adder #(.width(16)) adder_8 (.a(A), .b(adder_5_out), .out(adder_8_out), .cout(adder_8_cout));  // open: cin
  Adder #(.width(16)) adder_9 (.a(A), .b(16'h1), .out(adder_9_out), .cout(adder_9_cout));  // open: cin
  Adder #(.width(16)) adder_10 (.a(A), .b(adder_6_out), .out(adder_10_out), .cout(adder_10_cout));  // open: cin
  nor nor_2 (nor_2_out, adder_10_cout, adder_6_cout);
  nor nor_3 (nor_3_out, adder_7_cout, adder_4_cout);
  nor nor_4 (nor_4_out, adder_8_cout, adder_5_cout);
  PLA #(.in_width(5), .out_width(6), .\table ("00000 000000 # CLR\n10000 000000 # SER\n00001 000001 # NOT\n10001 000101 # TWO\n00010 000001 # AND\n10010 000001 # NAND\n00011 000001 # OR\n10011 000001 # NOR\n00100 000001 # XOR\n10100 000001 # XNOR\n00101 000011 # ADD\n10101 000011 # ADC\n00110 000111 # SUB\n10110 000111 # SBC\n00111 000011 # INC\n10111 000111 # DEC\n01000 000001 # MOV\n11000 000001 # MVN\n01001 000000 # SET\n11001 000000 # STN\n01010 000111 # CMP")) pla_1 (
    .in({Op[0], Op[4:1]}), .out(pla_1_out));
  not not_5 (not_5_out, En);
  Multiplexer #(.enable("false"), .select(5), .width(16)) multiplexer_1 (
    .in0({16{1'b0}}), .in1({16{1'b1}}), .in2(not_1_out), .in3(adder_1_out), .in4(and_1_out),
    .in5(nand_1_out), .in6(or_1_out), .in7(nor_1_out), .in8(xor_1_out), .in9(xnor_1_out), .in10(adder_2_out),
    .in11(adder_3_out), .in12(adder_7_out), .in13(adder_8_out), .in14(adder_9_out), .in15(adder_10_out),
    .in16(B), .in17({16{1'b0}}), .in18({16{1'b0}}), .in19({16{1'b0}}), .in20({16{1'b0}}), .in21({16{1'b0}}),
    .in22({16{1'b0}}), .in23({16{1'b0}}), .in24({16{1'b0}}), .in25({16{1'b0}}), .in26({16{1'b0}}),
    .in27({16{1'b0}}), .in28({16{1'b0}}), .in29({16{1'b0}}), .in30({16{1'b0}}), .in31({16{1'b0}}),
    .out(multiplexer_1_out), .sel(Op));
  BitFinder #(.width(16)) bitfinder_1 (.in(multiplexer_1_out), .found(bitfinder_1_found));  // open: index
  Pull_Resistor pull_resistor_1 (.node(Q));
  and and_2 (and_2_out[0], pla_1_out[0], ~bitfinder_1_found);  // AND_Gate
  Transistor #(.width(16)) transistor_1 (.in(multiplexer_1_out), .out(Q), .gate(not_5_out));
  and and_3 (and_2_out[1], pla_1_out[1], multiplexer_2_out);
  and and_4 (and_2_out[2], pla_1_out[2], multiplexer_3_out);
  PLA #(.in_width(5), .out_width(4), .\table ("00101 0001 # ADD (ADD)\n10101 0010 # ADC (ADC)\n00110 0011 # SUB (SUB)\n10110 0100 # SBC (SBC)\n00111 0001 # INC (ADD)\n10111 0011 # DEC (SUB)\n01010 0011 # CMP (SUB)\nxxxxx 0000 # X")) pla_2 (
    .in(Op), .out(pla_2_out));
  Multiplexer #(.enable("false"), .select(4)) multiplexer_2 (
    .in0(1'b0), .in1(adder_2_cout), .in2(adder_3_cout), .in3(adder_7_cout), .in4(adder_8_cout),
    .in5(adder_9_cout), .in6(adder_10_cout), .in7(1'b0), .in8(1'b0), .in9(1'b0), .in10(1'b0), .in11(1'b0),
    .in12(1'b0), .in13(1'b0), .in14(1'b0), .in15(1'b0), .out(multiplexer_2_out), .sel(pla_2_out));
  Pull_Resistor pull_resistor_2 (.node(Flg));
  Transistor #(.gate("br"), .width(6)) transistor_2 (.in({3'b000, and_2_out}), .out(Flg), .gate(not_5_out));
  PLA #(.in_width(5), .out_width(4), .\table ("00110 0001 # SUB (SUB)\n10110 0010 # SBC (SBC)\n10111 0001 # DEC (SUB)\n01010 0001 # CMP (SUB)\nxxxxx 0000 # X")) pla_3 (
    .in(Op), .out(pla_3_out));
  Multiplexer #(.enable("false"), .select(4)) multiplexer_3 (
    .in0(1'b0), .in1(nor_3_out), .in2(nor_4_out), .in3(nor_2_out), .in4(1'b0), .in5(1'b0), .in6(1'b0),
    .in7(1'b0), .in8(1'b0), .in9(1'b0), .in10(1'b0), .in11(1'b0), .in12(1'b0), .in13(1'b0), .in14(1'b0),
    .in15(1'b0), .out(multiplexer_3_out), .sel(pla_3_out));

  // Notes on the sheet:
  //   CLR
  //   SER
  //   AND
  //   NAND
  //   NOR
  //   XNOR
  //   SBC
  //   NOT
  //   TWO
  //   OR
  //   XOR
  //   ADD
  //   ADC
  //   SUB
  //   A - B -> D
  //   A - (B + C) -> D
  //   INC
  //   DEC
  //   CMP
  //   NOTE: First and last bit in opcode are swapped!!!!
  //   Instruction Flags
  //   Result Selection
  //   Carry Flag Selection
  //   Z
  //   C
  //   T
  //   Twos Flag Selection
endmodule

module ALUDecoder (
  input  [31:0] Ins,
  output FlagEn,
  output [4:0] Op,
  output [3:0] rA,
  output [3:0] rB,
  output IEn,
  output [3:0] rD,
  output [15:0] Im
);

  Multiplexer #(.enable("false"), .width(4)) multiplexer_1 (.in0(Ins[19:16]), .in1(Ins[15:12]), .out(rD), .sel(Ins[1]));

  assign FlagEn = Ins[2];
  assign IEn = Ins[1];
  assign Im = Ins[31:16];
  assign Op = Ins[7:3];
  assign rA = Ins[11:8];
  assign rB = Ins[15:12];

  // Notes on the sheet:
  //   Data
  //   Use Immediate
  //   No Flags
  //   Op Code
  //   rA
  //   rB/rD
  //   rD/Immediate
endmodule

module MemIO (
  input  MDn,
  input  [15:0] MDout,
  input  [15:0] Addr,
  input  [15:0] DIn,
  input  Read,
  input  Write,
  input  En,
  input  Clk,
  output Done,
  output [15:0] DOut,
  output [15:0] MAddr,
  output [15:0] MDin,
  output MR,
  output MW,
  output MEn,
  output MClk
);

  Transistor #(.gate("br"), .\type ("n"), .width(16)) transistor_1 (.in(MDout), .out(DOut), .gate(En));
  and and_1 (MR, Read, En);
  and and_2 (MW, Write, En);

  assign Done = MDn;
  assign MAddr = Addr;
  assign MClk = Clk;
  assign MDin = DIn;
  assign MEn = En;

  // Notes on the sheet:
  //   DOut: pull=up
endmodule
